// Logisim project Project3Given.circ as structural Verilog: 10 circuits, main circuit CPU15
module main (
  input  EnableBreakpoint,
  input  [14:0] Breakpoint
);

  wire and_2_out, and_3_out, chipset_1_irq, CLK, clock_1_out, cpu15_1_c, cpu15_1_e, cpu15_1_i, cpu15_1_n,
       cpu15_1_o, cpu15_1_z, KBCLR, KBIRQ, KBRD, MEMCS, nand_1_out, RE, TTYCLR, TTYWE, WE;
  wire [6:0] KBDATA, TTYDATA;
  wire [7:0] cpu15_1_srf;
  wire [14:0] ADDR, chipset_1_ivect, chipset_1_led0, chipset_1_led1, chipset_1_led2, chipset_1_led3,
       chipset_1_led4, chipset_1_led5, chipset_1_led6, chipset_1_led7, chipset_1_led8, chipset_1_led9,
       chipset_1_leda, chipset_1_ledb, chipset_1_ledc, chipset_1_ledd, chipset_1_lede, cpu15_1_ib,
       cpu15_1_pc, cpu15_1_r0, cpu15_1_r1, cpu15_1_r2, cpu15_1_r3, cpu15_1_r4, cpu15_1_r5, cpu15_1_r6,
       cpu15_1_r7, cpu15_1_srp, DATA, xnor_1_out;

  Clock clock_1 (.out(clock_1_out));
  nand nand_1 (nand_1_out, EnableBreakpoint, xnor_1_out[0], xnor_1_out[1], xnor_1_out[2], xnor_1_out[3], xnor_1_out[4], xnor_1_out[5], xnor_1_out[6], xnor_1_out[7], xnor_1_out[8], xnor_1_out[9], xnor_1_out[10], xnor_1_out[11], xnor_1_out[12], xnor_1_out[13], xnor_1_out[14], 1'b1);
  and and_1 (CLK, clock_1_out, nand_1_out);
  assign xnor_1_out = ~(Breakpoint ^ cpu15_1_pc);  // XNOR_Gate xnor_1, 15 bits wide
  LED I (.in(cpu15_1_i));
  LED Z (.in(cpu15_1_z));
  LED N (.in(cpu15_1_n));
  LED O (.in(cpu15_1_o));
  LED C (.in(cpu15_1_c));
  LED E (.in(cpu15_1_e));
  and and_2 (and_2_out, WE, MEMCS);
  and and_3 (and_3_out, MEMCS, RE);
  RAM #(.addrWidth(15), .asyncread("true"), .dataWidth(15), .databus("bidir")) ram_1 (
    .addr(ADDR), .we(and_2_out), .oe(and_3_out), .clk(CLK), .data(DATA));
  // Probe on cpu15_1_pc
  // Probe on cpu15_1_ib
  // Probe on cpu15_1_srp
  // Probe on cpu15_1_srf
  // Probe on cpu15_1_r0
  // Probe on cpu15_1_r1
  // Probe on cpu15_1_r2
  // Probe on cpu15_1_r3
  // Probe on cpu15_1_r4
  // Probe on cpu15_1_r5
  // Probe on cpu15_1_r6
  // Probe on cpu15_1_r7
  CPU15 cpu15_1 (
    .I(cpu15_1_i), .Z(cpu15_1_z), .N(cpu15_1_n), .O(cpu15_1_o), .C(cpu15_1_c), .E(cpu15_1_e),
    .PC(cpu15_1_pc), .IB(cpu15_1_ib), .SRP(cpu15_1_srp), .SRF(cpu15_1_srf), .R0(cpu15_1_r0), .R1(cpu15_1_r1),
    .R2(cpu15_1_r2), .R3(cpu15_1_r3), .R4(cpu15_1_r4), .R5(cpu15_1_r5), .R6(cpu15_1_r6), .R7(cpu15_1_r7),
    .CLK(CLK), .IRQ(chipset_1_irq), .RE(RE), .WE(WE), .ADDR(ADDR), .DATAIN(DATA), .DATAOUT(DATA));
  // Probe on ADDR
  // Probe on DATA
  // Probe on chipset_1_ivect
  // Probe on TTYDATA
  CHIPSET chipset_1 (
    .RE(RE), .WE(WE), .ADDR(ADDR), .CPUDATAIN(DATA), .CPUDATAOUT(DATA), .IRQ(chipset_1_irq),
    .IVECT(chipset_1_ivect), .CLK(CLK), .MEMCS(MEMCS), .TTYWR(TTYWE), .TTYCLR(TTYCLR), .TTYDATA(TTYDATA),
    .KBRD(KBRD), .KBCLR(KBCLR), .KBIRQ(KBIRQ), .KBDATA(KBDATA), .LED0(chipset_1_led0), .LED1(chipset_1_led1),
    .LED2(chipset_1_led2), .LED3(chipset_1_led3), .LED4(chipset_1_led4), .LED5(chipset_1_led5),
    .LED6(chipset_1_led6), .LED7(chipset_1_led7), .LED8(chipset_1_led8), .LED9(chipset_1_led9),
    .LEDA(chipset_1_leda), .LEDB(chipset_1_ledb), .LEDC(chipset_1_ledc), .LEDD(chipset_1_ledd),
    .LEDE(chipset_1_lede));
  TTY tty_1 (.data(TTYDATA), .clk(CLK), .we(TTYWE), .clr(TTYCLR));
  Keyboard keyboard_1 (.clk(CLK), .re(KBRD), .clr(KBCLR), .avail(KBIRQ), .data(KBDATA));
  DotMatrix #(.matrixcols(15), .matrixrows(15)) dotmatrix_1 (
    .col0(chipset_1_led0), .col1(chipset_1_led1), .col2(chipset_1_led2), .col3(chipset_1_led3),
    .col4(chipset_1_led4), .col5(chipset_1_led5), .col6(chipset_1_led6), .col7(chipset_1_led7),
    .col8(chipset_1_led8), .col9(chipset_1_led9), .col10(chipset_1_leda), .col11(chipset_1_ledb),
    .col12(chipset_1_ledc), .col13(chipset_1_ledd), .col14(chipset_1_lede));
endmodule

// CPU
module CPU15 (
  input  [14:0] DATAIN,
  input  CLK,
  input  IRQ,
  output [14:0] PC,
  output [14:0] IB,
  output [14:0] SRP,
  output [7:0] SRF,
  output [14:0] R0,
  output [14:0] R1,
  output [14:0] R2,
  output [14:0] R3,
  output [14:0] R4,
  output [14:0] R5,
  output [14:0] R6,
  output [14:0] R7,
  output RE,
  output WE,
  output I,
  output Z,
  output [14:0] ADDR,
  output N,
  output O,
  output C,
  output E,
  output [14:0] DATAOUT
);

  wire BR_TAKEN, BRANCH, decoder_1_out16, decoder_1_out17, decoder_1_out18, decoder_1_out19, decoder_1_out20,
       decoder_1_out21, JAL, JALR, load, multiplexer_5_out, not_1_out, not_2_out, not_3_out, not_4_out,
       or_1_out, regw, stage, store;
  wire [1:0] asel, bsel, flagsrc;
  wire [2:0] aluop, regwsrc;
  wire [3:0] ALUFlags;
  wire [7:0] and_2_out, bit_extender_1_out, flagwm, nf;
  wire [7:4] flags8_1_f;
  wire [14:0] adder15_2_s, ALURes, DATA, DATAOUT_t, F15, multiplexer_1_out, multiplexer_2_out,
       multiplexer_3_out, multiplexer_4_out, multiplexer_7_out, multiplexer_8_out, NextPC, rdata1, sext;

  or or_1 (or_1_out, JALR, JAL, BR_TAKEN);
  Multiplexer #(.select(3), .width(15)) multiplexer_1 (
    .in0(ALURes), .in1(sext), .in2(F15), .in5(DATA), .out(multiplexer_1_out), .sel(regwsrc));  // open: in3, in4, in6, in7
  Decoder #(.enable("false"), .select(5)) decoder_1 (
    .out16(decoder_1_out16), .out17(decoder_1_out17), .out18(decoder_1_out18), .out19(decoder_1_out19),
    .out20(decoder_1_out20), .out21(decoder_1_out21), .out27(JALR), .out28(JAL), .sel(IB[4:0]));  // open: out0, out1, out2, out3, out4, out5, out6, out7, out8, out9, out10, out11, out12, out13, out14, out15, out22, out23, out24, out25, out26, out29, out30, out31
  Multiplexer #(.width(15)) multiplexer_2 (.in0(15'h1), .in1(sext), .out(multiplexer_2_out), .sel(or_1_out));
  ADDER15 adder15_1 (.A(multiplexer_3_out), .B(multiplexer_2_out), .CIN(1'b0), .S(NextPC));  // open: COUT
  Multiplexer #(.width(15)) multiplexer_3 (.in0(PC), .in1(rdata1), .out(multiplexer_3_out), .sel(JALR));
  Register #(.width(15)) PC_r (.D(NextPC), .en(stage), .clk(CLK), .Q(PC));  // open: clr
  assign DATA = RE ? DATAIN : 15'bz;  // Controlled_Buffer controlled_buffer_1
  IMM15 imm15_1 (.INST(IB), .SEXT(sext));
  or or_2 (BRANCH, decoder_1_out16, decoder_1_out17, decoder_1_out18, decoder_1_out19, decoder_1_out20, decoder_1_out21);
  not not_1 (not_1_out, Z);
  not not_2 (not_2_out, N);
  not not_3 (not_3_out, C);
  assign DATAOUT = WE ? DATAOUT_t : 15'bz;  // Controlled_Buffer controlled_buffer_2
  Multiplexer #(.width(15)) multiplexer_4 (.in0(DATA), .in1({15{1'b0}}), .out(multiplexer_4_out), .sel(stage));
  REGS15 regs15_1 (
    .D(multiplexer_1_out), .W(regw), .SelD(IB[7:5]), .CLK(CLK), .SelA(IB[10:8]), .SelB(IB[13:11]), .R0(R0),
    .R1(R1), .R2(R2), .R3(R3), .R4(R4), .R5(R5), .R6(R6), .R7(R7), .A(rdata1), .B(DATAOUT_t));
  Multiplexer #(.select(3)) multiplexer_5 (
    .in0(Z), .in1(not_1_out), .in2(N), .in3(not_2_out), .in4(C), .in5(not_3_out), .out(multiplexer_5_out),
    .sel(IB[2:0]));  // open: in6, in7
  ADDER15 adder15_2 (.A(rdata1), .B(sext), .CIN(1'b0), .S(adder15_2_s));  // open: COUT
  Register #(.width(15)) IB_r (.D(multiplexer_4_out), .en(1'b1), .clk(CLK), .Q(IB));  // open: clr
  and and_1 (BR_TAKEN, BRANCH, multiplexer_5_out);
  assign and_2_out = flagwm & bit_extender_1_out;  // AND_Gate and_2, 8 bits wide
  assign bit_extender_1_out = {{7{stage}}, stage};  // Bit_Extender bit_extender_1
  Multiplexer #(.width(15)) multiplexer_6 (.in0(PC), .in1(adder15_2_s), .out(ADDR), .sel(stage));
  Register #(.width(1)) u_stage (.D(not_4_out), .en(1'b1), .clk(CLK), .Q(stage));  // open: clr
  not not_4 (not_4_out, stage);
  Multiplexer #(.select(2), .width(15)) multiplexer_7 (
    .in0(DATAOUT_t), .in1(sext), .in2(15'h1), .out(multiplexer_7_out), .sel(bsel));  // open: in3
  Multiplexer #(.select(2), .width(15)) multiplexer_8 (
    .in0(rdata1), .in1(PC), .out(multiplexer_8_out), .sel(asel));  // open: in2, in3
  FLAGS8 flags8_1 (.NF(nf), .WM(and_2_out), .CLK(CLK), .IRQ(IRQ), .F({flags8_1_f[7], I, E, flags8_1_f[4], O, C, N, Z}));
  ALU15 alu15_1 (
    .A(multiplexer_8_out), .B(multiplexer_7_out), .OP(aluop), .CIN(1'b0), .OIN(1'b0), .R(ALURes),
    .C(ALUFlags[2]), .O(ALUFlags[3]), .N(ALUFlags[1]), .Z(ALUFlags[0]));
  Multiplexer multiplexer_9 (.in0(1'b1), .in1(load), .out(RE), .sel(stage));
  assign F15 = {{7{1'b0}}, {flags8_1_f[7], I, E, flags8_1_f[4], O, C, N, Z}};  // Bit_Extender bit_extender_2
  Multiplexer #(.select(2), .width(8)) multiplexer_10 (
    .in0({4'b0000, ALUFlags}), .in1(rdata1[7:0]), .in2({8{1'b0}}), .out(nf), .sel(flagsrc));  // open: in3
  DECODE15 decode15_1 (
    .OPCODE(IB[4:0]), .STORE(store), .LOAD(load), .ASEL(asel), .BSEL(bsel), .ALUOP(aluop),
    .REGDATASRC(regwsrc), .REGW(regw), .FLAGSRC(flagsrc), .FLAGWM(flagwm));  // open: SWI, SRPW, SRFW
  Multiplexer multiplexer_11 (.in0(1'b0), .in1(store), .out(WE), .sel(stage));

  // Other names for the same wires on the sheet: opcode[4:0] = IB[4:0]; rd[2:0] = IB[7:5]; rs1[2:0] = IB[10:8];
  //   rs2[2:0] = IB[13:11]; rdata2[14:0] = DATAOUT_t
endmodule

module CHIPSET (
  input  RE,
  input  WE,
  input  [14:0] ADDR,
  input  [14:0] CPUDATAIN,
  input  KBIRQ,
  input  [6:0] KBDATA,
  input  CLK,
  output MEMCS,
  output TTYWR,
  output [14:0] IVECT,
  output TTYCLR,
  output [6:0] TTYDATA,
  output KBRD,
  output KBCLR,
  output [14:0] CPUDATAOUT,
  output IRQ,
  output [14:0] LED0,
  output [14:0] LED1,
  output [14:0] LED2,
  output [14:0] LED3,
  output [14:0] LED4,
  output [14:0] LED5,
  output [14:0] LED6,
  output [14:0] LED7,
  output [14:0] LED8,
  output [14:0] LED9,
  output [14:0] LEDA,
  output [14:0] LEDB,
  output [14:0] LEDC,
  output [14:0] LEDD,
  output [14:0] LEDE
);

  wire and_1_out, and_8_out, and_10_out, DATA7, IOCS, IVECTADDR, IVECTEN, IVECTRE, KBCS, LED0EN, LED0END,
       LED1EN, LED1END, LED2EN, LED2END, LED3EN, LED3END, LED4EN, LED4END, LED5EN, LED5END, LED6EN, LED6END,
       LED7EN, LED7END, LED8EN, LED8END, LED9EN, LED9END, LEDAEN, LEDAEND, LEDBEN, LEDBEND, LEDCEN, LEDCEND,
       LEDCS, LEDDEN, LEDDEND, LEDEEN, LEDEEND, LEDFEND, LEDRE, multiplexer_17_out, multiplexer_18_out, RWE,
       TTYCS;
  wire [14:0] DATAL0, DATAL1, DATAL2, DATAL3, DATAL4, DATAL5, DATAL6, DATAL7, DATAL8, DATAL9, DATALA, DATALB,
       DATALC, DATALD, DATALE, LEDDATA;
  wire [14:8] KBDATA15;

  assign CPUDATAOUT = KBRD ? {KBDATA15, DATA7, KBDATA} : 15'bz;  // Controlled_Buffer controlled_buffer_1
  assign CPUDATAOUT = LEDRE ? LEDDATA : 15'bz;  // Controlled_Buffer controlled_buffer_2
  assign CPUDATAOUT = IVECTRE ? IVECT : 15'bz;  // Controlled_Buffer controlled_buffer_3
  Register #(.width(15)) register_1 (.D(DATAL0), .en(LED0EN), .Q(LED0), .clk(CLK));  // open: clr
  Register #(.width(15)) register_2 (.D(DATAL1), .en(LED1EN), .Q(LED1), .clk(CLK));  // open: clr
  Register #(.width(15)) register_3 (.D(DATAL2), .en(LED2EN), .Q(LED2), .clk(CLK));  // open: clr
  Register #(.width(15)) register_4 (.D(DATAL3), .en(LED3EN), .Q(LED3), .clk(CLK));  // open: clr
  Register #(.width(15)) register_5 (.D(DATAL4), .en(LED4EN), .Q(LED4), .clk(CLK));  // open: clr
  and and_1 (and_1_out, WE, LEDCS);
  Decoder #(.select(4)) decoder_1 (
    .out0(LED0END), .out1(LED1END), .out2(LED2END), .out3(LED3END), .out4(LED4END), .out5(LED5END),
    .out6(LED6END), .out7(LED7END), .out8(LED8END), .out9(LED9END), .out10(LEDAEND), .out11(LEDBEND),
    .out12(LEDCEND), .out13(LEDDEND), .out14(LEDEEND), .out15(LEDFEND), .sel(ADDR[3:0]), .en(and_1_out));
  Register #(.width(15)) register_6 (.D(DATAL5), .en(LED5EN), .Q(LED5), .clk(CLK));  // open: clr
  Register #(.width(15)) register_7 (.D(DATAL6), .en(LED6EN), .Q(LED6), .clk(CLK));  // open: clr
  Register #(.width(15)) register_8 (.D(DATAL7), .en(LED7EN), .Q(LED7), .clk(CLK));  // open: clr
  Register #(.width(15)) register_9 (.D(DATAL8), .en(LED8EN), .Q(LED8), .clk(CLK));  // open: clr
  Register #(.width(15)) register_10 (.D(DATAL9), .en(LED9EN), .Q(LED9), .clk(CLK));  // open: clr
  or or_1 (LED0EN, LED0END, LEDFEND);
  or or_2 (LED1EN, LED1END, LEDFEND);
  or or_3 (LED2EN, LED2END, LEDFEND);
  or or_4 (LED3EN, LED3END, LEDFEND);
  or or_5 (LED4EN, LED4END, LEDFEND);
  or or_6 (LED5EN, LED5END, LEDFEND);
  or or_7 (LED6EN, LED6END, LEDFEND);
  or or_8 (LED7EN, LED7END, LEDFEND);
  or or_9 (LED8EN, LED8END, LEDFEND);
  or or_10 (LED9EN, LED9END, LEDFEND);
  or or_11 (LEDAEN, LEDAEND, LEDFEND);
  or or_12 (LEDBEN, LEDBEND, LEDFEND);
  or or_13 (LEDCEN, LEDCEND, LEDFEND);
  or or_14 (LEDDEN, LEDDEND, LEDFEND);
  or or_15 (LEDEEN, LEDEEND, LEDFEND);
  Pull_Resistor pull_resistor_1 (.node(KBDATA15[14]));
  Pull_Resistor pull_resistor_2 (.node(KBDATA15[13]));
  Pull_Resistor pull_resistor_3 (.node(KBDATA15[12]));
  Pull_Resistor pull_resistor_4 (.node(KBDATA15[11]));
  Pull_Resistor pull_resistor_5 (.node(KBDATA15[10]));
  Pull_Resistor pull_resistor_6 (.node(KBDATA15[9]));
  Pull_Resistor pull_resistor_7 (.node(KBDATA15[8]));
  Pull_Resistor pull_resistor_8 (.node(DATA7));
  Register #(.width(15)) register_11 (.D(DATALA), .en(LEDAEN), .Q(LEDA), .clk(CLK));  // open: clr
  Register #(.width(15)) register_12 (.D(DATALB), .en(LEDBEN), .Q(LEDB), .clk(CLK));  // open: clr
  Register #(.width(15)) register_13 (.D(DATALC), .en(LEDCEN), .Q(LEDC), .clk(CLK));  // open: clr
  Register #(.width(15)) register_14 (.D(DATALD), .en(LEDDEN), .Q(LEDD), .clk(CLK));  // open: clr
  Register #(.width(15)) register_15 (.D(DATALE), .en(LEDEEN), .Q(LEDE), .clk(CLK));  // open: clr
  Multiplexer #(.width(15)) multiplexer_1 (.in0(CPUDATAIN), .in1(LED1), .out(DATAL0), .sel(LEDFEND));
  Multiplexer #(.width(15)) multiplexer_2 (.in0(CPUDATAIN), .in1(LED2), .out(DATAL1), .sel(LEDFEND));
  Multiplexer #(.width(15)) multiplexer_3 (.in0(CPUDATAIN), .in1(LED3), .out(DATAL2), .sel(LEDFEND));
  Multiplexer #(.width(15)) multiplexer_4 (.in0(CPUDATAIN), .in1(LED4), .out(DATAL3), .sel(LEDFEND));
  Multiplexer #(.width(15)) multiplexer_5 (.in0(CPUDATAIN), .in1(LED5), .out(DATAL4), .sel(LEDFEND));
  Multiplexer #(.select(4), .width(15)) multiplexer_6 (
    .in0(LED0), .in1(LED1), .in2(LED2), .in3(LED3), .in4(LED4), .in5(LED5), .in6(LED6), .in7(LED7),
    .in8(LED8), .in9(LED9), .in10(LEDA), .in11(LEDB), .in12(LEDC), .in13(LEDD), .in14(LEDE),
    .in15({15{1'b0}}), .out(LEDDATA), .sel(ADDR[3:0]));
  Multiplexer #(.width(15)) multiplexer_7 (.in0(CPUDATAIN), .in1(LED6), .out(DATAL5), .sel(LEDFEND));
  Multiplexer #(.width(15)) multiplexer_8 (.in0(CPUDATAIN), .in1(LED7), .out(DATAL6), .sel(LEDFEND));
  Multiplexer #(.width(15)) multiplexer_9 (.in0(CPUDATAIN), .in1(LED8), .out(DATAL7), .sel(LEDFEND));
  Multiplexer #(.width(15)) multiplexer_10 (.in0(CPUDATAIN), .in1(LED9), .out(DATAL8), .sel(LEDFEND));
  Multiplexer #(.width(15)) multiplexer_11 (.in0(CPUDATAIN), .in1(LEDA), .out(DATAL9), .sel(LEDFEND));
  and and_2 (LEDRE, RE, LEDCS);
  Multiplexer #(.width(15)) multiplexer_12 (.in0(CPUDATAIN), .in1(LEDB), .out(DATALA), .sel(LEDFEND));
  Multiplexer #(.width(15)) multiplexer_13 (.in0(CPUDATAIN), .in1(LEDC), .out(DATALB), .sel(LEDFEND));
  Multiplexer #(.width(15)) multiplexer_14 (.in0(CPUDATAIN), .in1(LEDD), .out(DATALC), .sel(LEDFEND));
  Multiplexer #(.width(15)) multiplexer_15 (.in0(CPUDATAIN), .in1(LEDE), .out(DATALD), .sel(LEDFEND));
  Multiplexer #(.width(15)) multiplexer_16 (.in0(CPUDATAIN), .in1(CPUDATAIN), .out(DATALE), .sel(LEDFEND));
  and and_3 (IOCS, ADDR[5], ADDR[6], ADDR[7], ADDR[8], ADDR[9], ADDR[10], ADDR[11], ADDR[12], ADDR[13], ADDR[14], 1'b1);
  and and_4 (TTYCS, IOCS, ADDR[0], ~ADDR[1], ~ADDR[2], ~ADDR[3], ADDR[4]);  // AND_Gate
  and and_5 (KBCS, IOCS, ~ADDR[0], ~ADDR[1], ~ADDR[2], ~ADDR[3], ADDR[4]);  // AND_Gate
  and and_6 (IVECTADDR, ADDR[0], ADDR[1], ADDR[2], ADDR[3], ADDR[4], ADDR[5], ADDR[6], ADDR[7], ADDR[8], ADDR[9], ADDR[10], ADDR[11], ADDR[12], ADDR[13], ADDR[14]);
  and and_7 (TTYWR, TTYCS, WE);
  and and_8 (and_8_out, TTYWR, DATA7);
  and and_9 (KBRD, KBCS, RE);
  and and_10 (and_10_out, KBCS, WE);
  Multiplexer multiplexer_17 (.in0(and_10_out), .in1(1'b0), .out(multiplexer_17_out), .sel(KBCLR));
  and and_11 (LEDCS, IOCS, ~ADDR[4], RWE);  // AND_Gate
  and and_12 (IVECTEN, IVECTADDR, WE);
  and and_13 (IVECTRE, IVECTADDR, RE);
  or or_16 (RWE, RE, WE);
  and and_14 (MEMCS, ~IOCS, RWE);  // AND_Gate
  Multiplexer multiplexer_18 (.in0(and_8_out), .in1(1'b0), .out(multiplexer_18_out), .sel(TTYCLR));
  D_Flip_Flop d_ff_1 (.clk(CLK), .D(multiplexer_17_out), .Q(KBCLR));  // open: Qn, preset, reset
  Register #(.width(15)) register_16 (.D(CPUDATAIN), .en(IVECTEN), .Q(IVECT), .clk(CLK));  // open: clr
  D_Flip_Flop d_ff_2 (.clk(CLK), .D(multiplexer_18_out), .Q(TTYCLR));  // open: Qn, preset, reset

  assign IRQ = KBIRQ;
  assign TTYDATA = CPUDATAIN[6:0];

  // Other names for the same wires on the sheet: DATA[14:0] = CPUDATAIN; KBDATA15[7:0] = {DATA7, KBDATA}
endmodule

module ADDER15 (
  input  [14:0] A,
  input  [14:0] B,
  input  CIN,
  output COUT,
  output [14:0] S
);

  wire cla5_1_cout, cla5_2_cout;

  CLA5 cla5_1 (
    .A0(A[0]), .A1(A[1]), .A2(A[2]), .A3(A[3]), .A4(A[4]), .B0(B[0]), .B1(B[1]), .B2(B[2]), .B3(B[3]),
    .B4(B[4]), .CIN(CIN), .S0(S[0]), .S1(S[1]), .S2(S[2]), .S3(S[3]), .S4(S[4]), .COUT(cla5_1_cout));
  CLA5 cla5_2 (
    .A0(A[5]), .A1(A[6]), .A2(A[7]), .A3(A[8]), .A4(A[9]), .B0(B[5]), .B1(B[6]), .B2(B[7]), .B3(B[8]),
    .B4(B[9]), .CIN(cla5_1_cout), .S0(S[5]), .S1(S[6]), .S2(S[7]), .S3(S[8]), .S4(S[9]), .COUT(cla5_2_cout));
  CLA5 cla5_3 (
    .A0(A[10]), .A1(A[11]), .A2(A[12]), .A3(A[13]), .A4(A[14]), .B0(B[10]), .B1(B[11]), .B2(B[12]),
    .B3(B[13]), .B4(B[14]), .CIN(cla5_2_cout), .S0(S[10]), .S1(S[11]), .S2(S[12]), .S3(S[13]), .S4(S[14]),
    .COUT(COUT));
endmodule

module REGS15 (
  input  [14:0] D,
  input  W,
  input  [2:0] SelD,
  input  CLK,
  input  [2:0] SelA,
  input  [2:0] SelB,
  output [14:0] R0,
  output [14:0] R1,
  output [14:0] R2,
  output [14:0] R3,
  output [14:0] R4,
  output [14:0] R5,
  output [14:0] R6,
  output [14:0] R7,
  output [14:0] A,
  output [14:0] B
);

  wire and_1_out, and_2_out, and_3_out, and_4_out, and_5_out, and_6_out, and_7_out, decoder_1_out1,
       decoder_1_out2, decoder_1_out3, decoder_1_out4, decoder_1_out5, decoder_1_out6, decoder_1_out7;

  Decoder #(.enable("false"), .select(3)) decoder_1 (
    .out1(decoder_1_out1), .out2(decoder_1_out2), .out3(decoder_1_out3), .out4(decoder_1_out4),
    .out5(decoder_1_out5), .out6(decoder_1_out6), .out7(decoder_1_out7), .sel(SelD));  // open: out0
  and and_1 (and_1_out, decoder_1_out1, W);
  and and_2 (and_2_out, decoder_1_out2, W);
  and and_3 (and_3_out, decoder_1_out3, W);
  and and_4 (and_4_out, decoder_1_out4, W);
  and and_5 (and_5_out, decoder_1_out5, W);
  and and_6 (and_6_out, decoder_1_out6, W);
  and and_7 (and_7_out, decoder_1_out7, W);
  Register #(.width(15)) register_1 (.D(D), .en(and_1_out), .clk(CLK), .Q(R1));  // open: clr
  Register #(.width(15)) register_2 (.D(D), .en(and_2_out), .clk(CLK), .Q(R2));  // open: clr
  Register #(.width(15)) register_3 (.D(D), .en(and_3_out), .clk(CLK), .Q(R3));  // open: clr
  Register #(.width(15)) register_4 (.D(D), .en(and_4_out), .clk(CLK), .Q(R4));  // open: clr
  Register #(.width(15)) register_5 (.D(D), .en(and_5_out), .clk(CLK), .Q(R5));  // open: clr
  Register #(.width(15)) register_6 (.D(D), .en(and_6_out), .clk(CLK), .Q(R6));  // open: clr
  Register #(.width(15)) register_7 (.D(D), .en(and_7_out), .clk(CLK), .Q(R7));  // open: clr
  Multiplexer #(.select(3), .width(15)) multiplexer_1 (
    .in0({15{1'b0}}), .in1(R1), .in2(R2), .in3(R3), .in4(R4), .in5(R5), .in6(R6), .in7(R7), .out(A),
    .sel(SelA));
  Multiplexer #(.select(3), .width(15)) multiplexer_2 (
    .in0({15{1'b0}}), .in1(R1), .in2(R2), .in3(R3), .in4(R4), .in5(R5), .in6(R6), .in7(R7), .out(B),
    .sel(SelB));

  assign R0 = {15{1'b0}};
endmodule

module ALU15 (
  input  [14:0] A,
  input  [14:0] B,
  input  [2:0] OP,
  input  CIN,
  input  OIN,
  output C,
  output O,
  output N,
  output Z,
  output [14:0] R
);

  wire and_2_out, or_1_out, xnor_1_out, xor_2_out, xor_3_out, xor_4_out, xor_5_out;
  wire [14:0] adder15_1_s, and_1_out, or_2_out, shifter_1_out, shifter_2_out, shifter_3_out, xor_1_out;

  or or_1 (or_1_out, R[0], R[1], R[2], R[3], R[4], R[5], R[6], R[7], R[8], R[9], R[10], R[11], R[12], R[13], N);
  not not_1 (Z, or_1_out);
  ADDER15 adder15_1 (.A(A), .B(B), .CIN(OP[0]), .COUT(C), .S(adder15_1_s));
  assign and_1_out = A & B;  // AND_Gate and_1, 15 bits wide
  assign or_2_out = A | B;  // OR_Gate or_2, 15 bits wide
  assign xor_1_out = A ^ B;  // XOR_Gate xor_1, 15 bits wide
  Shifter #(.width(15)) shifter_1 (.in(A), .\dist (B[3:0]), .out(shifter_1_out));
  Shifter #(.shift("lr"), .width(15)) shifter_2 (.in(A), .\dist (B[3:0]), .out(shifter_2_out));
  Shifter #(.shift("ar"), .width(15)) shifter_3 (.in(A), .\dist (B[3:0]), .out(shifter_3_out));
  Multiplexer #(.select(3), .width(15)) multiplexer_1 (
    .in0(adder15_1_s), .in1(adder15_1_s), .in2(and_1_out), .in3(or_2_out), .in4(xor_1_out),
    .in5(shifter_1_out), .in6(shifter_2_out), .in7(shifter_3_out), .out({N, R[13:0]}), .sel(OP));
  xor xor_2 (xor_2_out, A[14], N);
  xor xor_3 (xor_3_out, A[14], B[14]);
  xor xor_4 (xor_4_out, A[14], N);
  xnor xnor_1 (xnor_1_out, A[14], B[14]);
  and and_2 (and_2_out, xor_2_out, xnor_1_out);
  xor xor_5 (xor_5_out, xor_3_out, xor_4_out);
  Multiplexer #(.select(3)) multiplexer_2 (
    .in0(and_2_out), .in1(xor_5_out), .out(O), .sel(OP));  // open: in2, in3, in4, in5, in6, in7

  assign R[14] = N;

  // Other names for the same wires on the sheet: sub = OP[0]
endmodule

module FLAGS8 (
  input  IRQ,
  input  [7:0] NF,
  input  [7:0] WM,
  input  CLK,
  output [7:0] F
);

  wire or_1_out, or_2_out;

  Register #(.width(1)) Z (.D(NF[0]), .en(WM[0]), .clk(CLK), .Q(F[0]));  // open: clr
  Register #(.width(1)) N (.D(NF[1]), .en(WM[1]), .clk(CLK), .Q(F[1]));  // open: clr
  Register #(.width(1)) C (.D(NF[2]), .en(WM[2]), .clk(CLK), .Q(F[2]));  // open: clr
  Register #(.width(1)) O (.D(NF[3]), .en(WM[3]), .clk(CLK), .Q(F[3]));  // open: clr
  Register #(.width(1)) E (.D(NF[5]), .en(WM[5]), .clk(CLK), .Q(F[5]));  // open: clr
  or or_1 (or_1_out, IRQ, NF[6]);
  Register #(.width(1)) I (.D(or_1_out), .en(or_2_out), .clk(CLK), .Q(F[6]));  // open: clr
  or or_2 (or_2_out, IRQ, WM[6]);

  assign {F[7], F[4]} = 2'b00;

  // Other names for the same wires on the sheet: Z = F[0]; N = F[1]; C = F[2]; O = F[3]; E = F[5]; I = F[6];
  //   NZ = NF[0]; NN = NF[1]; NC = NF[2]; NO = NF[3]; NE = NF[5]; NI = NF[6]; WZ = WM[0]; WN = WM[1]; WC = WM[2];
  //   WO = WM[3]; WE = WM[5]; WI = WM[6]
endmodule

module IMM15 (
  input  [14:0] INST,
  output [14:0] SEXT
);

  wire Cimm_3_0, Cimm_6_0, Cimm_9_0, CLUI, CSW, decoder_1_out8, decoder_1_out9, decoder_1_out10,
       decoder_1_out11, decoder_1_out12, decoder_1_out13, decoder_1_out14, decoder_1_out15, decoder_1_out16,
       decoder_1_out17, decoder_1_out18, decoder_1_out19, decoder_1_out20, decoder_1_out21, decoder_1_out27,
       decoder_1_out28, decoder_1_out29;
  wire [14:0] imm_3_0, imm_6_0, imm_9_0, imm_LUI, imm_SW, multiplexer_1_out, multiplexer_2_out,
       multiplexer_3_out, multiplexer_4_out;

  Decoder #(.enable("false"), .select(5)) decoder_1 (
    .out8(decoder_1_out8), .out9(decoder_1_out9), .out10(decoder_1_out10), .out11(decoder_1_out11),
    .out12(decoder_1_out12), .out13(decoder_1_out13), .out14(decoder_1_out14), .out15(decoder_1_out15),
    .out16(decoder_1_out16), .out17(decoder_1_out17), .out18(decoder_1_out18), .out19(decoder_1_out19),
    .out20(decoder_1_out20), .out21(decoder_1_out21), .out27(decoder_1_out27), .out28(decoder_1_out28),
    .out29(decoder_1_out29), .out30(CSW), .out31(CLUI), .sel(INST[4:0]));  // open: out0, out1, out2, out3, out4, out5, out6, out7, out22, out23, out24, out25, out26
  Multiplexer #(.width(15)) multiplexer_1 (.in0({15{1'b0}}), .in1(imm_SW), .out(multiplexer_1_out), .sel(CSW));
  or or_1 (Cimm_3_0, decoder_1_out8, decoder_1_out9, decoder_1_out10, decoder_1_out11, decoder_1_out12, decoder_1_out13, decoder_1_out14, decoder_1_out15, decoder_1_out27);
  or or_2 (Cimm_9_0, decoder_1_out16, decoder_1_out17, decoder_1_out18, decoder_1_out19, decoder_1_out20, decoder_1_out21);
  or or_3 (Cimm_6_0, decoder_1_out28, decoder_1_out29);
  Multiplexer #(.width(15)) multiplexer_2 (.in0(multiplexer_1_out), .in1(imm_LUI), .out(multiplexer_2_out), .sel(CLUI));
  Multiplexer #(.width(15)) multiplexer_3 (
    .in0(multiplexer_2_out), .in1(imm_6_0), .out(multiplexer_3_out), .sel(Cimm_6_0));
  assign imm_3_0 = {{11{INST[14]}}, INST[14:11]};  // Bit_Extender bit_extender_1
  assign imm_9_0 = {{5{INST[14]}}, INST[14:5]};  // Bit_Extender bit_extender_2
  assign imm_6_0 = {{8{INST[14]}}, INST[14:8]};  // Bit_Extender bit_extender_3
  assign imm_LUI = {{4{INST[14]}}, {INST[14:8], 4'b0000}};  // Bit_Extender bit_extender_4
  assign imm_SW = {{11{INST[14]}}, {INST[14], INST[7:5]}};  // Bit_Extender bit_extender_5
  Multiplexer #(.width(15)) multiplexer_4 (
    .in0(multiplexer_3_out), .in1(imm_9_0), .out(multiplexer_4_out), .sel(Cimm_9_0));
  Multiplexer #(.width(15)) multiplexer_5 (.in0(multiplexer_4_out), .in1(imm_3_0), .out(SEXT), .sel(Cimm_3_0));

  // Other names for the same wires on the sheet: OP[4:0] = INST[4:0]
endmodule

module DECODE15 (
  input  [4:0] OPCODE,
  output SWI,
  output STORE,
  output LOAD,
  output [1:0] ASEL,
  output [1:0] BSEL,
  output [2:0] ALUOP,
  output [2:0] REGDATASRC,
  output REGW,
  output [1:0] FLAGSRC,
  output [7:0] FLAGWM,
  output SRPW,
  output SRFW
);

  wire ADD, ADDI, and_1_out, and_2_out, JAL, JALR, LUI, not_1_out, not_2_out, not_3_out, not_4_out,
       not_5_out, not_6_out, or_1_out, or_2_out, RTI, SF, SFI, SSRF, SSRP, SUB;

  Decoder #(.enable("false"), .select(5)) decoder_1 (
    .out0(ADD), .out1(SUB), .out8(ADDI), .out9(LOAD), .out22(RTI), .out23(SWI), .out24(SSRP), .out25(SSRF),
    .out26(SF), .out27(JALR), .out28(JAL), .out29(SFI), .out30(STORE), .out31(LUI), .sel(OPCODE));  // open: out2, out3, out4, out5, out6, out7, out10, out11, out12, out13, out14, out15, out16, out17, out18, out19, out20, out21
  not not_1 (not_1_out, OPCODE[4]);
  and and_1 (and_1_out, not_1_out, not_2_out);
  not not_2 (not_2_out, LOAD);
  not not_3 (not_3_out, OPCODE[4]);
  not not_4 (not_4_out, OPCODE[4]);
  not not_5 (not_5_out, OPCODE[4]);
  not not_6 (not_6_out, OPCODE[4]);
  and and_2 (and_2_out, not_3_out, OPCODE[3]);
  or or_1 (or_1_out, JALR, JAL);
  or or_2 (or_2_out, JALR, JAL);
  or or_3 (REGW, not_4_out, SSRP, SSRF, SF, JALR, JAL, SFI, LUI);
  or or_4 (SRPW, SWI, SSRP);
  or or_5 (SRFW, SWI, SSRF);
  Priority_Encoder priority_encoder_1 (
    .in0(1'b1), .in1(LUI), .in2(SF), .in3(SSRP), .in4(SSRF), .in5(LOAD), .out(REGDATASRC), .en_in(1'b1));  // open: in6, in7, gs, en_out
  Priority_Encoder #(.select(2)) priority_encoder_2 (
    .in0(and_1_out), .in1(SF), .in2(SWI), .in3(RTI), .out(FLAGSRC), .en_in(1'b1));  // open: gs, en_out
  or or_6 (FLAGWM[5], SWI, RTI, SF);
  or or_7 (FLAGWM[0], not_5_out, RTI, SF);
  or or_8 (FLAGWM[1], not_6_out, RTI, SF);
  or or_9 (FLAGWM[3], ADD, SUB, ADDI, RTI, SF);
  Priority_Encoder #(.select(2)) priority_encoder_3 (
    .in0(1'b1), .in1(and_2_out), .in2(or_1_out), .out(BSEL), .en_in(1'b1));  // open: in3, gs, en_out
  Priority_Encoder #(.select(2)) priority_encoder_4 (
    .in0(1'b1), .in1(or_2_out), .out(ASEL), .en_in(1'b1));  // open: in2, in3, gs, en_out

  assign ALUOP = OPCODE[2:0];
  assign {FLAGWM[7:6], FLAGWM[4], FLAGWM[2]} = {3'b000, FLAGWM[3]};

  // Other names for the same wires on the sheet: FLAGMZ = FLAGWM[0]; FLAGMN = FLAGWM[1]; FLAGMC = FLAGWM[3];
  //   FLAGMO = FLAGWM[3]; FLAGME = FLAGWM[5]
endmodule

module CLA5 (
  input  A0,
  input  A1,
  input  A2,
  input  A3,
  input  A4,
  input  B0,
  input  B1,
  input  B2,
  input  B3,
  input  B4,
  input  CIN,
  output S0,
  output S1,
  output S2,
  output S3,
  output S4,
  output COUT
);

  wire and_2_out, and_3_out, and_4_out, and_5_out, and_6_out, and_7_out, and_10_out, and_11_out, and_12_out,
       and_13_out, and_15_out, and_16_out, and_17_out, and_18_out, and_19_out, C0, C1, C2, C3, G0, G1, G2,
       G3, G4, P0, P1, P2, P3, P4;

  and and_1 (G0, A0, B0);
  or or_1 (P0, A0, B0);
  xor xor_1 (S0, A0, B0, CIN);
  or or_2 (C0, G0, and_2_out);
  and and_2 (and_2_out, P0, CIN);
  and and_3 (and_3_out, G0, P1);
  and and_4 (and_4_out, P1, P0, CIN);
  and and_5 (and_5_out, P2, G1);
  and and_6 (and_6_out, P2, P1, G0);
  and and_7 (and_7_out, P2, P1, P0, CIN);
  or or_3 (C1, G1, and_3_out, and_4_out);
  or or_4 (C2, G2, and_5_out, and_6_out, and_7_out);
  and and_8 (G1, A1, B1);
  or or_5 (P1, A1, B1);
  xor xor_2 (S1, A1, B1, C0);
  and and_9 (G2, A2, B2);
  or or_6 (P2, A2, B2);
  and and_10 (and_10_out, P3, G2);
  and and_11 (and_11_out, P3, P2, G1);
  and and_12 (and_12_out, P3, P2, P1, G0);
  and and_13 (and_13_out, P3, P2, P1, P0, CIN);
  xor xor_3 (S2, A2, B2, C1);
  or or_7 (C3, G3, and_10_out, and_11_out, and_12_out, and_13_out);
  and and_14 (G3, A3, B3);
  or or_8 (P3, A3, B3);
  xor xor_4 (S3, A3, B3, C2);
  and and_15 (and_15_out, P4, G3);
  and and_16 (and_16_out, P4, P3, G2);
  and and_17 (and_17_out, P4, P3, P2, G1);
  and and_18 (and_18_out, P4, P3, P2, P1, G0);
  and and_19 (and_19_out, P4, P3, P2, P1, P0, CIN);
  and and_20 (G4, A4, B4);
  or or_9 (P4, A4, B4);
  xor xor_5 (S4, A4, B4, C3);
  or or_10 (COUT, G4, and_15_out, and_16_out, and_17_out, and_18_out, and_19_out);

  // Other names for the same wires on the sheet: C4 = COUT
endmodule
